# Fritzing sketch Sketch1 (saved by Fritzing 0.9.4)
breadboards: 1

parts:
  Part1 = Arduino Mega 2560 (Rev3)
  Pololu_A1 = Pololu A4988 [package=SO16]
  LCD2004-I2C1 = LCD2004-I2C
  kEYPAD_MATRICIAL_1 = KEYPAD 4x3  # not connected
  ZS-042_RTC1 = ZS-042 RTC Module
  microSD1 = MicroSD Card Module  # not connected
  U1 = LIPO-2000mAh [package=lipo-2000]
  M1 = Stepper Motor - Bipolar
  C1 = Electrolytic Capacitor [capacitance=0.1mF voltage=16V package="100 mil [THT, electrolytic]"]

nets:
  N1: Part1.D21/SCL, Part1.SCL, LCD2004-I2C1.SCL, ZS-042_RTC1.SCL
  N2: Part1.D20/SDA, Part1.SDA, LCD2004-I2C1.SDA, ZS-042_RTC1.SDA
  VCC: Part1.5V, Pololu_A1.VDD, LCD2004-I2C1.VCC, ZS-042_RTC1.VCC
  GND: Part1.GND, Pololu_A1.GND#8, LCD2004-I2C1.GND, ZS-042_RTC1.GND
  N3: Pololu_A1.1B, M1.A
  N4: Pololu_A1.1A, M1.C
  N5: Pololu_A1.2A, M1.B
  N6: Pololu_A1.2B, M1.D
  N7: Pololu_A1.GND#14, U1.-, C1.-
  N8: Pololu_A1.VMOT, U1.+, C1.+

custom parts:
  LCD2004-I2C: A standard character display with 4x20 characters. Comes in many colors with LCM2004 IIC attached.
  KEYPAD 4x3: KEYPAD matricial de 12 botones, 4 filas x 3 columnas
